# Fritzing sketch touchpad-piano (saved by Fritzing 0.9.6b)
breadboards: 1

parts:
  Piano1 = Touchpad Piano
  Pro_Micro1 = SparkFun Pro Micro

nets:
  GND: Piano1.GND, Pro_Micro1.GND
  VCC: Piano1.VCC, Pro_Micro1.VCC
  N1: Piano1.SCL, Pro_Micro1.3
  N2: Piano1.SDO, Pro_Micro1.2

custom parts:
  Touchpad Piano: A Touchpad piano module
  SparkFun Pro Micro: The Pro Micro is similar to the Pro Mini except with an ATmega32U4 on board. The USB transceiver inside the 32U4 allows us to add USB connectivity on-board and do away with bulky external USB interface. Based on: https://github.com/unorthodox-engineers/unorthodox-arduino/blob/master/Unorthodox/fritzing/parts/Pro%20Micro.fzpz

// code stored in the sketch: touchpad-piano.ino
#include <USB-MIDI.h>

USBMIDI_CREATE_DEFAULT_INSTANCE();


#define SCL_PIN 3
#define SDO_PIN 2

#define MIDI_CHANNEL 1


byte NOTE_POS[12] = {1,3,6,8,10,0,2,4,5,7,9,11};
byte keys_state[12] = {0};

void setup()
{
  /* Initialise the serial interface */
  Serial.begin(9600);
  /* Configure the clock and data pins */
  pinMode(SCL_PIN, OUTPUT);
  pinMode(SDO_PIN, INPUT);
  
  MIDI.begin(MIDI_CHANNEL_OMNI);
  
//  while (!Serial); // Leonardo: wait for Serial Monitor

}

void loop()
{
  byte new_keys_state[12];
  byte i;

  // Read data
  for (i = 0; i < 12; i++)
  {
    digitalWrite(SCL_PIN, LOW);
    new_keys_state[NOTE_POS[i]] = !digitalRead(SDO_PIN);
    digitalWrite(SCL_PIN, HIGH);
  }

  // Display data
  for (i = 0; i < 12; i++)
  {
    Serial.print(new_keys_state[i]);
    if (new_keys_state[i] != keys_state[i])
    {
      if (new_keys_state[i] == 1)
        MIDI.sendNoteOn(60 + i, 64, MIDI_CHANNEL);
      else
        MIDI.sendNoteOff(60 + i, 64, MIDI_CHANNEL);
        
      keys_state[i] = new_keys_state[i];
    }
  }

  Serial.println();

  delay(100);
}
